// Logisim project one_cpu.circ as structural Verilog: 11 circuits, main circuit main
module main (
  input  in_1,
  output [31:0] out_2,
  output out_3,
  output [4:0] out_4,
  output [31:0] out_5,
  output out_6,
  output [4:0] out_7,
  output [31:0] out_8
);

  wire ALUSrc, beq, clock_1_out, ExtOp, MemtoReg, RegDst, zero;
  wire [2:0] controller_1_aluctr;
  wire [31:0] alu_1_c, ext_1_out_3, grf_1_rd1, multiplexer_2_out, ram_1_data;

  IFU ifu_1 (.imm16(out_2[15:0]), .Ifbeq(beq), .zero(zero), .reset(in_1), .Instr(out_2));
  Controller controller_1 (
    .opcode(out_2[31:26]), .func(out_2[5:0]), .RegDst(RegDst), .ALUSrc(ALUSrc), .MemtoReg(MemtoReg),
    .RegWrite(out_3), .MemWrite(out_6), .nPC_sel(beq), .ExtOp(ExtOp), .ALUCtr(controller_1_aluctr));
  Multiplexer #(.width(5)) multiplexer_1 (
    .in0(out_2[20:16]), .in1(out_2[15:11]), .out(out_4), .sel(RegDst));  // open: en
  GRF grf_1 (
    .A1(out_2[25:21]), .A2(out_2[20:16]), .A3(out_4), .data(out_5), .WE(out_3), .in_6(in_1), .RD1(grf_1_rd1),
    .RD2(out_8));
  EXT ext_1 (.in_2(out_2[15:0]), .ExtOp(ExtOp), .out_3(ext_1_out_3));
  Multiplexer #(.width(32)) multiplexer_2 (
    .in0(out_8), .in1(ext_1_out_3), .out(multiplexer_2_out), .sel(ALUSrc));  // open: en
  ALU alu_1 (.A(grf_1_rd1), .B(multiplexer_2_out), .Zero(zero), .C(alu_1_c), .ALUCtr(controller_1_aluctr));
  _32to5 u_32to5_1 (.in_1(alu_1_c), .out_2(out_7));
  Clock clock_1 (.out(clock_1_out));
  RAM #(.addrWidth(5), .dataWidth(32), .bus("separate")) ram_1 (
    .addr(out_7), .din(out_8), .data(ram_1_data), .str(out_6), .clk(clock_1_out), .ld(MemtoReg));  // open: sel, clr
  Multiplexer #(.width(32)) multiplexer_3 (.in0(alu_1_c), .in1(ram_1_data), .out(out_5), .sel(MemtoReg));  // open: en

  // Other names for the same wires on the sheet: Instr[31:0] = out_2; imm16[15:0] = out_2[15:0]; MemAddr[4:0] = out_7;
  //   MemData[31:0] = out_8; MemWrite = out_6; RegAddr[4:0] = out_4; RegData[31:0] = out_5; RegWrite = out_3;
  //   Reset = in_1
endmodule

// grf
module GRF (
  input  WE,
  input  [4:0] A1,
  input  [4:0] A2,
  input  [4:0] A3,
  input  [31:0] data,
  input  in_6,
  output [31:0] RD1,
  output [31:0] RD2
);

  wire clock_1_out, decoder_1_out1, decoder_1_out2, decoder_1_out3, decoder_1_out4, decoder_1_out5,
       decoder_1_out6, decoder_1_out7, decoder_1_out8, decoder_1_out9, decoder_1_out10, decoder_1_out11,
       decoder_1_out12, decoder_1_out13, decoder_1_out14, decoder_1_out15, decoder_1_out16, decoder_1_out17,
       decoder_1_out18, decoder_1_out19, decoder_1_out20, decoder_1_out21, decoder_1_out22, decoder_1_out23,
       decoder_1_out24, decoder_1_out25, decoder_1_out26, decoder_1_out27, decoder_1_out28, decoder_1_out29,
       decoder_1_out30, decoder_1_out31;
  wire [4:0] multiplexer_1_out;
  wire [31:0] _0, _1, _2, _3, _4, _5, _6, _7, _8, _9, _10, _11, _12, _13, _14, _15, _16, _17, _18, _19, _20,
       _21, _22, _23, _24, _25, _26, _27, _28, _29, _30, _31;

  Multiplexer #(.width(5)) multiplexer_1 (.in0({5{1'b0}}), .in1(A3), .out(multiplexer_1_out), .sel(WE));  // open: en
  Decoder #(.select(5)) decoder_1 (
    .out1(decoder_1_out1), .out2(decoder_1_out2), .out3(decoder_1_out3), .out4(decoder_1_out4),
    .out5(decoder_1_out5), .out6(decoder_1_out6), .out7(decoder_1_out7), .out8(decoder_1_out8),
    .out9(decoder_1_out9), .out10(decoder_1_out10), .out11(decoder_1_out11), .out12(decoder_1_out12),
    .out13(decoder_1_out13), .out14(decoder_1_out14), .out15(decoder_1_out15), .out16(decoder_1_out16),
    .out17(decoder_1_out17), .out18(decoder_1_out18), .out19(decoder_1_out19), .out20(decoder_1_out20),
    .out21(decoder_1_out21), .out22(decoder_1_out22), .out23(decoder_1_out23), .out24(decoder_1_out24),
    .out25(decoder_1_out25), .out26(decoder_1_out26), .out27(decoder_1_out27), .out28(decoder_1_out28),
    .out29(decoder_1_out29), .out30(decoder_1_out30), .out31(decoder_1_out31), .sel(multiplexer_1_out));  // open: out0, en
  Clock clock_1 (.out(clock_1_out));
  Register #(.width(32)) u__0 (.Q(_0), .clk(clock_1_out), .clr(in_6));  // open: D, en
  Register #(.width(32)) u__1 (.D(data), .en(decoder_1_out1), .Q(_1), .clk(clock_1_out), .clr(in_6));
  Register #(.width(32)) u__2 (.D(data), .en(decoder_1_out2), .Q(_2), .clk(clock_1_out), .clr(in_6));
  Register #(.width(32)) u__3 (.D(data), .en(decoder_1_out3), .Q(_3), .clk(clock_1_out), .clr(in_6));
  Register #(.width(32)) u__4 (.D(data), .en(decoder_1_out4), .Q(_4), .clk(clock_1_out), .clr(in_6));
  Register #(.width(32)) u__5 (.D(data), .en(decoder_1_out5), .Q(_5), .clk(clock_1_out), .clr(in_6));
  Register #(.width(32)) u__6 (.D(data), .en(decoder_1_out6), .Q(_6), .clk(clock_1_out), .clr(in_6));
  Register #(.width(32)) u__7 (.D(data), .en(decoder_1_out7), .Q(_7), .clk(clock_1_out), .clr(in_6));
  Register #(.width(32)) u__8 (.D(data), .en(decoder_1_out8), .Q(_8), .clk(clock_1_out), .clr(in_6));
  Register #(.width(32)) u__9 (.D(data), .en(decoder_1_out9), .Q(_9), .clk(clock_1_out), .clr(in_6));
  Register #(.width(32)) u__10 (.D(data), .en(decoder_1_out10), .Q(_10), .clk(clock_1_out), .clr(in_6));
  Register #(.width(32)) u__11 (.D(data), .en(decoder_1_out11), .Q(_11), .clk(clock_1_out), .clr(in_6));
  Register #(.width(32)) u__12 (.D(data), .en(decoder_1_out12), .Q(_12), .clk(clock_1_out), .clr(in_6));
  Register #(.width(32)) u__13 (.D(data), .en(decoder_1_out13), .Q(_13), .clk(clock_1_out), .clr(in_6));
  Register #(.width(32)) u__14 (.D(data), .en(decoder_1_out14), .Q(_14), .clk(clock_1_out), .clr(in_6));
  Register #(.width(32)) u__15 (.D(data), .en(decoder_1_out15), .Q(_15), .clk(clock_1_out), .clr(in_6));
  Register #(.width(32)) u__16 (.D(data), .en(decoder_1_out16), .Q(_16), .clk(clock_1_out), .clr(in_6));
  Register #(.width(32)) u__17 (.D(data), .en(decoder_1_out17), .Q(_17), .clk(clock_1_out), .clr(in_6));
  Register #(.width(32)) u__18 (.D(data), .en(decoder_1_out18), .Q(_18), .clk(clock_1_out), .clr(in_6));
  Register #(.width(32)) u__19 (.D(data), .en(decoder_1_out19), .Q(_19), .clk(clock_1_out), .clr(in_6));
  Register #(.width(32)) u__20 (.D(data), .en(decoder_1_out20), .Q(_20), .clk(clock_1_out), .clr(in_6));
  Register #(.width(32)) u__21 (.D(data), .en(decoder_1_out21), .Q(_21), .clk(clock_1_out), .clr(in_6));
  Register #(.width(32)) u__22 (.D(data), .en(decoder_1_out22), .Q(_22), .clk(clock_1_out), .clr(in_6));
  Register #(.width(32)) u__23 (.D(data), .en(decoder_1_out23), .Q(_23), .clk(clock_1_out), .clr(in_6));
  Register #(.width(32)) u__24 (.D(data), .en(decoder_1_out24), .Q(_24), .clk(clock_1_out), .clr(in_6));
  Register #(.width(32)) u__25 (.D(data), .en(decoder_1_out25), .Q(_25), .clk(clock_1_out), .clr(in_6));
  Register #(.width(32)) u__26 (.D(data), .en(decoder_1_out26), .Q(_26), .clk(clock_1_out), .clr(in_6));
  Register #(.width(32)) u__27 (.D(data), .en(decoder_1_out27), .Q(_27), .clk(clock_1_out), .clr(in_6));
  Register #(.width(32)) u__28 (.D(data), .en(decoder_1_out28), .Q(_28), .clk(clock_1_out), .clr(in_6));
  Register #(.width(32)) u__29 (.D(data), .en(decoder_1_out29), .Q(_29), .clk(clock_1_out), .clr(in_6));
  Register #(.width(32)) u__30 (.D(data), .en(decoder_1_out30), .Q(_30), .clk(clock_1_out), .clr(in_6));
  Register #(.width(32)) u__31 (.D(data), .en(decoder_1_out31), .Q(_31), .clk(clock_1_out), .clr(in_6));
  Multiplexer #(.select(5), .width(32)) multiplexer_2 (
    .in0(_0), .in1(_1), .in2(_2), .in3(_3), .in4(_4), .in5(_5), .in6(_6), .in7(_7), .in8(_8), .in9(_9),
    .in10(_10), .in11(_11), .in12(_12), .in13(_13), .in14(_14), .in15(_15), .in16(_16), .in17(_17),
    .in18(_18), .in19(_19), .in20(_20), .in21(_21), .in22(_22), .in23(_23), .in24(_24), .in25(_25),
    .in26(_26), .in27(_27), .in28(_28), .in29(_29), .in30(_30), .in31(_31), .out(RD1), .sel(A1));  // open: en
  Multiplexer #(.select(5), .width(32)) multiplexer_3 (
    .in0(_0), .in1(_1), .in2(_2), .in3(_3), .in4(_4), .in5(_5), .in6(_6), .in7(_7), .in8(_8), .in9(_9),
    .in10(_10), .in11(_11), .in12(_12), .in13(_13), .in14(_14), .in15(_15), .in16(_16), .in17(_17),
    .in18(_18), .in19(_19), .in20(_20), .in21(_21), .in22(_22), .in23(_23), .in24(_24), .in25(_25),
    .in26(_26), .in27(_27), .in28(_28), .in29(_29), .in30(_30), .in31(_31), .out(RD2), .sel(A2));  // open: en

  // Other names for the same wires on the sheet: reset = in_6
endmodule

// alu
module ALU (
  input  [2:0] ALUCtr,
  input  [31:0] A,
  input  [31:0] B,
  output Zero,
  output [31:0] C
);

  wire comparator_1_eq, not_1_out, not_2_out;
  wire [31:0] adder_1_out, or_1_out, shifter_1_out, subtractor_1_out;

  Adder #(.width(32)) adder_1 (.a(A), .b(B), .out(adder_1_out));  // open: cin, cout
  Subtractor #(.width(32)) subtractor_1 (.a(A), .b(B), .out(subtractor_1_out));  // open: bin, bout
  assign or_1_out = A | B;  // OR_Gate or_1, 32 bits wide
  Shifter #(.width(32)) shifter_1 (.in(B), .\dist (5'b10000), .out(shifter_1_out));
  not not_1 (not_1_out, ALUCtr[0]);
  not not_2 (not_2_out, ALUCtr[2]);
  Multiplexer #(.select(3), .width(32)) multiplexer_1 (
    .in0(adder_1_out), .in1(subtractor_1_out), .in2(subtractor_1_out), .in3(or_1_out), .in4(shifter_1_out),
    .out(C), .sel(ALUCtr));  // open: in5, in6, in7, en
  Comparator #(.width(32)) comparator_1 (.a({32{1'b0}}), .b(C), .eq(comparator_1_eq));  // open: gt, lt
  and and_1 (Zero, not_1_out, ALUCtr[1], not_2_out, comparator_1_eq);
endmodule

module IFU (
  input  [15:0] imm16,
  input  Ifbeq,
  input  zero,
  input  reset,
  output [31:0] Instr
);

  wire [31:0] npc_1_newpc, pc_1_out_3;

  NPC npc_1 (.oldpc(pc_1_out_3), .imm16(imm16), .Ifbeq(Ifbeq), .zero(zero), .newpc(npc_1_newpc));
  PC pc_1 (.in_1(npc_1_newpc), .reset(reset), .out_3(pc_1_out_3));
  IM im_1 (.pc(pc_1_out_3), .out_2(Instr));
endmodule

// npc
module NPC (
  input  [31:0] oldpc,
  input  [15:0] imm16,
  input  Ifbeq,
  input  zero,
  output [31:0] newpc
);

  wire and_1_out;
  wire [31:0] adder_1_out, adder_2_out, shifter_1_out, sign_extend_1_out_2;

  sign_extend sign_extend_1 (.in_1(imm16), .out_2(sign_extend_1_out_2));
  and and_1 (and_1_out, Ifbeq, zero);
  Shifter #(.width(32)) shifter_1 (.in(sign_extend_1_out_2), .\dist (5'b00010), .out(shifter_1_out));
  Adder #(.width(32)) adder_1 (.a(32'h4), .b(oldpc), .out(adder_1_out));  // open: cin, cout
  Adder #(.width(32)) adder_2 (.a(adder_1_out), .b(shifter_1_out), .out(adder_2_out));  // open: cin, cout
  Multiplexer #(.width(32)) multiplexer_1 (
    .in0(adder_1_out), .in1(adder_2_out), .out(newpc), .sel(and_1_out));  // open: en
endmodule

// pc
module PC (
  input  [31:0] in_1,
  input  reset,
  output [31:0] out_3
);

  wire clock_1_out;

  Clock clock_1 (.out(clock_1_out));
  Register #(.width(32)) pc (.D(in_1), .Q(out_3), .clk(clock_1_out), .clr(reset));  // open: en
endmodule

// signext
module sign_extend (
  input  [15:0] in_1,
  output [31:0] out_2
);


  assign out_2 = {{17{in_1[15]}}, in_1[14:0]};
endmodule

// im
module IM (
  input  [31:0] pc,
  output [31:0] out_2
);

  ROM #(.addrWidth(5), .dataWidth(32)) rom_1 (.addr(pc[6:2]), .data(out_2));  // open: sel

  // Notes on the sheet:
  //   contents of rom_1 (hex, n*v repeats v):
  //   34030008 32021 802823 10a40001 8c050000 3c060004 ac060004
endmodule

// controller
module Controller (
  input  [5:0] opcode,
  input  [5:0] func,
  output RegDst,
  output ALUSrc,
  output MemtoReg,
  output RegWrite,
  output MemWrite,
  output nPC_sel,
  output ExtOp,
  output [2:0] ALUCtr
);

  wire addu, beq, lui, lw, not_1_out, not_2_out, not_3_out, not_4_out, not_5_out, not_6_out, not_7_out,
       not_9_out, not_10_out, not_11_out, ori, subu, sw;

  not not_1 (not_1_out, opcode[1]);
  not not_2 (not_2_out, opcode[0]);
  not not_3 (not_3_out, opcode[2]);
  not not_4 (not_4_out, opcode[4]);
  not not_5 (not_5_out, opcode[3]);
  not not_6 (not_6_out, opcode[5]);
  not not_7 (not_7_out, func[1]);
  // NOT_Gate not_8 has open pins: in=func[0], out=open
  not not_9 (not_9_out, func[2]);
  not not_10 (not_10_out, func[3]);
  not not_11 (not_11_out, func[4]);
  // NOT_Gate not_12 has open pins: in=func[5], out=open
  and u_addu (addu, func[5], not_11_out, not_10_out, not_9_out, not_7_out, func[0], not_6_out, not_4_out, not_5_out, not_3_out, not_1_out, not_2_out);
  and u_subu (subu, func[5], not_11_out, not_10_out, not_9_out, func[1], func[0], not_6_out, not_4_out, not_5_out, not_3_out, not_1_out, not_2_out);
  and u_ori (ori, not_6_out, not_4_out, opcode[3], opcode[2], not_1_out, opcode[0]);
  and u_lw (lw, opcode[5], not_4_out, not_5_out, not_3_out, opcode[1], opcode[0]);
  and u_sw (sw, opcode[5], not_4_out, opcode[3], not_3_out, opcode[1], opcode[0]);
  and u_beq (beq, not_6_out, not_4_out, not_5_out, opcode[2], not_1_out, not_2_out);
  and u_lui (lui, not_6_out, not_4_out, opcode[3], opcode[2], opcode[1], opcode[0]);
  buf ALUCtr2 (ALUCtr[2], lui);  // OR_Gate
  or ALUCtr1 (ALUCtr[1], beq, ori);
  or ALUCtr0 (ALUCtr[0], subu, ori);
  or u_ExtOp (ExtOp, lw, lui, sw);
  buf u_nPC_sel (nPC_sel, beq);  // OR_Gate
  buf u_MemWrite (MemWrite, sw);  // OR_Gate
  or u_RegWrite (RegWrite, addu, subu, lui, ori, lw);
  buf u_MemtoReg (MemtoReg, lw);  // OR_Gate
  or u_ALUSrc (ALUSrc, ori, lw, lui, sw);
  or u_RegDst (RegDst, addu, subu);

  // Other names for the same wires on the sheet: fun0 = func[0]; fun1 = func[1]; fun2 = func[2]; fun3 = func[3];
  //   fun4 = func[4]; fun5 = func[5]; op0 = opcode[0]; op1 = opcode[1]; op2 = opcode[2]; op3 = opcode[3];
  //   op4 = opcode[4]; op5 = opcode[5]
endmodule

module _32to5 (
  input  [31:0] in_1,
  output [4:0] out_2
);


  assign out_2 = in_1[6:2];
endmodule

module EXT (
  input  ExtOp,
  input  [15:0] in_2,
  output [31:0] out_3
);

  wire [31:0] bit_extender_1_out, sign_extend_1_out_2;

  assign bit_extender_1_out = {{16{1'b0}}, in_2};  // Bit_Extender bit_extender_1
  sign_extend sign_extend_1 (.in_1(in_2), .out_2(sign_extend_1_out_2));
  Multiplexer #(.width(32)) multiplexer_1 (
    .in0(bit_extender_1_out), .in1(sign_extend_1_out_2), .out(out_3), .sel(ExtOp));  // open: en
endmodule
